// Logisim project stack_logical_normal.circ as structural Verilog: 12 circuits, main circuit main
module main (
  input  CLK,
  input  RESET,
  input  [1:0] COMMAND,
  input  [2:0] INDEX,
  input  [3:0] IO_DATA_in,
  output [3:0] IO_DATA_out
);

  wire [3:0] stack_1_d0, stack_1_d1, stack_1_d2, stack_1_d3, stack_1_d4;

  // Probe on stack_1_d4
  stack stack_1 (
    .CLK(CLK), .RESET(RESET), .COMMAND(COMMAND), .INDEX(INDEX), .IO_DATA_in(IO_DATA_in), .d4(stack_1_d4),
    .d3(stack_1_d3), .d2(stack_1_d2), .d1(stack_1_d1), .d0(stack_1_d0), .IO_DATA_out(IO_DATA_out));
  // Probe on stack_1_d3
  // Probe on stack_1_d2
  // Probe on stack_1_d1
  // Probe on stack_1_d0
endmodule

module stack (
  input  CLK,
  input  RESET,
  input  [1:0] COMMAND,
  input  [2:0] INDEX,
  input  [3:0] IO_DATA_in,
  output [3:0] d4,
  output [3:0] d3,
  output [3:0] d2,
  output [3:0] d1,
  output [3:0] d0,
  output [3:0] IO_DATA_out
);

  wire and_4_out, and_5_out, and_6_out, and_7_out, and_8_out, and_9_out, and_10_out, and_11_out, and_12_out,
       and_13_out, and_14_out, and_15_out, and_16_out, and_17_out, and_18_out, and_19_out, and_20_out,
       and_21_out, and_22_out, and_23_out, and_24_out, and_25_out, and_26_out, and_27_out, and_28_out,
       and_29_out, and_30_out, and_31_out, and_32_out, and_33_out, and_34_out, and_35_out, and_36_out,
       and_37_out, and_38_out, and_39_out, and_40_out, and_41_out, and_42_out, and_43_out, and_44_out,
       and_45_out, and_46_out, and_47_out, and_48_out, and_49_out, and_50_out, and_51_out, and_52_out,
       and_53_out, and_54_out, and_55_out, and_56_out, and_57_out, and_58_out, and_59_out, and_60_out,
       and_61_out, and_62_out, and_63_out, counter_mod5_1_q0, counter_mod5_1_q1, counter_mod5_1_q2,
       d0_output_time, d1_output_time, d2_output_time, d3_output_time, d4_output_time, decoder_4_1_z0,
       decoder_4_1_z1, decoder_4_1_z2, decoder_4_1_z3, get, get_pop_time, ind0, ind1, ind2, ind3, ind4, ind5,
       ind6, ind7, ind_0or5, ind_1or6, ind_2or7, nop, not_2_out, not_3_out, or_1_out, or_2_out, or_3_out,
       or_4_out, or_7_out, or_8_out, or_14_out, or_16_out, or_17_out, or_18_out, or_19_out, pop, push,
       push_pop_time, push_time, Z0, Z1, Z2, Z3, Z4;
  wire [3:0] DATA_out, not_1_out;

  assign not_1_out = ~DATA_out;  // NOT_Gate not_1, 4 bits wide
  not not_2 (not_2_out, get_pop_time);
  Transistor transistor_1 (.in(get_pop_time), .out(IO_DATA_in[3]), .gate(get_pop_time));
  Transistor #(.\type ("n")) transistor_2 (.in(not_2_out), .out(IO_DATA_in[3]), .gate(not_1_out[3]));
  Transistor transistor_3 (.in(get_pop_time), .out(IO_DATA_in[2]), .gate(not_1_out[3]));
  Transistor #(.\type ("n")) transistor_4 (.in(not_2_out), .out(IO_DATA_in[2]), .gate(not_1_out[3]));
  Transistor transistor_5 (.in(get_pop_time), .out(IO_DATA_in[1]), .gate(not_1_out[2]));
  Transistor #(.\type ("n")) transistor_6 (.in(not_2_out), .out(IO_DATA_in[1]), .gate(not_1_out[2]));
  Transistor transistor_7 (.in(get_pop_time), .out(IO_DATA_in[0]), .gate(not_1_out[1]));
  Transistor #(.\type ("n")) transistor_8 (.in(not_2_out), .out(IO_DATA_in[0]), .gate(not_1_out[1]));
  and and_1 (push_time, CLK, push);
  and and_2 (push_pop_time, CLK, or_1_out);
  or or_1 (or_1_out, pop, push);
  or or_2 (or_2_out, get, pop);
  and and_3 (get_pop_time, CLK, or_2_out);
  decoder_4 decoder_4_1 (
    .S1(COMMAND[1]), .S0(COMMAND[0]), .Z3(decoder_4_1_z3), .Z2(decoder_4_1_z2), .Z1(decoder_4_1_z1),
    .Z0(decoder_4_1_z0));
  not not_3 (not_3_out, CLK);
  decoder_8 decoder_8_2 (
    .S2(INDEX[2]), .S1(INDEX[1]), .S0(INDEX[0]), .Z7(ind7), .Z6(ind6), .Z5(ind5), .Z4(ind4), .Z3(ind3),
    .Z2(ind2), .Z1(ind1), .Z0(ind0));
  counter_mod5 counter_mod5_1 (
    .C(push_pop_time), .dec_inc(push), .RESET(RESET), .Q2(counter_mod5_1_q2), .Q1(counter_mod5_1_q1),
    .Q0(counter_mod5_1_q0));
  decoder_8 decoder_8_1 (
    .S2(counter_mod5_1_q2), .S1(counter_mod5_1_q1), .S0(counter_mod5_1_q0), .Z4(Z4), .Z3(Z3), .Z2(Z2),
    .Z1(Z1), .Z0(Z0));  // open: Z7, Z6, Z5
  D_register_4 d_register_4_1 (
    .D3(decoder_4_1_z3), .D2(decoder_4_1_z2), .D1(decoder_4_1_z1), .D0(decoder_4_1_z0), .C(not_3_out),
    .RESET(RESET), .out_8(get), .out_9(pop), .out_10(push), .out_11(nop));  // open: SET
  and and_4 (and_4_out, push_time, Z3);
  and and_5 (and_5_out, push_time, Z2);
  and and_6 (and_6_out, push_time, Z1);
  and and_7 (and_7_out, push_time, Z0);
  and and_8 (and_8_out, push_time, Z4);
  dynamic_D_register_4 D_register_4_1_dup2 (
    .D3(IO_DATA_in[3]), .D2(IO_DATA_in[2]), .D1(IO_DATA_in[1]), .D0(IO_DATA_in[0]), .C(and_4_out),
    .RESET(RESET), .Q3(d4[3]), .Q2(d4[2]), .Q1(d4[1]), .Q0(d4[0]));  // open: SET
  dynamic_D_register_4 D_register_4_2 (
    .D3(IO_DATA_in[3]), .D2(IO_DATA_in[2]), .D1(IO_DATA_in[1]), .D0(IO_DATA_in[0]), .C(and_5_out),
    .RESET(RESET), .Q3(d3[3]), .Q2(d3[2]), .Q1(d3[1]), .Q0(d3[0]));  // open: SET
  dynamic_D_register_4 D_register_4_4 (
    .D3(IO_DATA_in[3]), .D2(IO_DATA_in[2]), .D1(IO_DATA_in[1]), .D0(IO_DATA_in[0]), .C(and_6_out),
    .RESET(RESET), .Q3(d2[3]), .Q2(d2[2]), .Q1(d2[1]), .Q0(d2[0]));  // open: SET
  dynamic_D_register_4 D_register_4_5 (
    .D3(IO_DATA_in[3]), .D2(IO_DATA_in[2]), .D1(IO_DATA_in[1]), .D0(IO_DATA_in[0]), .C(and_7_out),
    .RESET(RESET), .Q3(d1[3]), .Q2(d1[2]), .Q1(d1[1]), .Q0(d1[0]));  // open: SET
  dynamic_D_register_4 D_register_4_6 (
    .D3(IO_DATA_in[3]), .D2(IO_DATA_in[2]), .D1(IO_DATA_in[1]), .D0(IO_DATA_in[0]), .C(and_8_out),
    .RESET(RESET), .Q3(d0[3]), .Q2(d0[2]), .Q1(d0[1]), .Q0(d0[0]));  // open: SET
  and and_9 (and_9_out, ind4, Z3);
  and and_10 (and_10_out, ind3, Z2);
  and and_11 (and_11_out, ind_2or7, Z1);
  and and_12 (and_12_out, ind_1or6, Z0);
  and and_13 (and_13_out, ind_0or5, Z4);
  and and_14 (and_14_out, ind4, Z0);
  and and_15 (and_15_out, ind3, Z4);
  and and_16 (and_16_out, ind_2or7, Z3);
  and and_17 (and_17_out, ind_1or6, Z2);
  and and_18 (and_18_out, ind_0or5, Z1);
  or or_3 (or_3_out, and_9_out, and_10_out, and_11_out, and_12_out, and_13_out);
  and and_19 (and_19_out, or_3_out, get);
  and and_20 (and_20_out, Z4, pop);
  or or_4 (or_4_out, and_14_out, and_15_out, and_16_out, and_17_out, and_18_out);
  and and_21 (and_21_out, or_4_out, get);
  and and_22 (and_22_out, Z1, pop);
  or or_5 (d4_output_time, and_19_out, and_20_out);
  or or_6 (d1_output_time, and_21_out, and_22_out);
  and and_23 (and_23_out, ind4, Z2);
  and and_24 (and_24_out, ind3, Z1);
  and and_25 (and_25_out, ind_2or7, Z0);
  and and_26 (and_26_out, ind_1or6, Z4);
  and and_27 (and_27_out, ind_0or5, Z3);
  and and_28 (and_28_out, ind4, Z4);
  and and_29 (and_29_out, ind3, Z3);
  and and_30 (and_30_out, ind_2or7, Z2);
  and and_31 (and_31_out, ind_1or6, Z1);
  and and_32 (and_32_out, ind_0or5, Z0);
  or or_7 (or_7_out, and_23_out, and_24_out, and_25_out, and_26_out, and_27_out);
  and and_33 (and_33_out, Z3, pop);
  or or_8 (or_8_out, and_28_out, and_29_out, and_30_out, and_31_out, and_32_out);
  and and_34 (and_34_out, Z0, pop);
  and and_35 (and_35_out, or_7_out, get);
  or or_9 (d3_output_time, and_35_out, and_33_out);
  and and_36 (and_36_out, or_8_out, get);
  or or_10 (d0_output_time, and_36_out, and_34_out);
  and and_37 (and_37_out, ind3, Z0);
  and and_38 (and_38_out, ind_2or7, Z4);
  and and_39 (and_39_out, ind_1or6, Z3);
  and and_40 (and_40_out, ind_0or5, Z2);
  or or_11 (ind_2or7, ind2, ind7);
  or or_12 (ind_1or6, ind1, ind6);
  or or_13 (ind_0or5, ind0, ind5);
  and and_41 (and_41_out, ind4, Z1);
  or or_14 (or_14_out, and_41_out, and_37_out, and_38_out, and_39_out, and_40_out);
  and and_42 (and_42_out, or_14_out, get);
  or or_15 (d2_output_time, and_42_out, and_43_out);
  and and_43 (and_43_out, Z2, pop);
  and and_44 (and_44_out, d4_output_time, d4[3]);
  and and_45 (and_45_out, d4_output_time, d4[2]);
  and and_46 (and_46_out, d4_output_time, d4[1]);
  and and_47 (and_47_out, d4_output_time, d4[0]);
  and and_48 (and_48_out, d3_output_time, d3[3]);
  and and_49 (and_49_out, d3_output_time, d3[2]);
  and and_50 (and_50_out, d3_output_time, d3[1]);
  and and_51 (and_51_out, d3_output_time, d3[0]);
  and and_52 (and_52_out, d2_output_time, d2[3]);
  and and_53 (and_53_out, d2_output_time, d2[2]);
  and and_54 (and_54_out, d2_output_time, d2[1]);
  and and_55 (and_55_out, d2_output_time, d2[0]);
  and and_56 (and_56_out, d1_output_time, d1[3]);
  and and_57 (and_57_out, d1_output_time, d1[2]);
  and and_58 (and_58_out, d1_output_time, d1[1]);
  and and_59 (and_59_out, d1_output_time, d1[0]);
  and and_60 (and_60_out, d0_output_time, d0[3]);
  and and_61 (and_61_out, d0_output_time, d0[2]);
  and and_62 (and_62_out, d0_output_time, d0[1]);
  and and_63 (and_63_out, d0_output_time, d0[0]);
  or or_16 (or_16_out, and_44_out, and_48_out, and_52_out, and_56_out, and_60_out);
  or or_17 (or_17_out, and_45_out, and_49_out, and_53_out, and_57_out, and_61_out);
  or or_18 (or_18_out, and_46_out, and_50_out, and_54_out, and_58_out, and_62_out);
  or or_19 (or_19_out, and_47_out, and_51_out, and_55_out, and_59_out, and_63_out);
  dynamic_D_register_4 dynamic_d_register_4_1 (
    .D3(or_16_out), .D2(or_17_out), .D1(or_18_out), .D0(or_19_out), .C(get_pop_time), .RESET(RESET),
    .Q3(DATA_out[3]), .Q2(DATA_out[2]), .Q1(DATA_out[1]), .Q0(DATA_out[0]));  // open: SET

  assign IO_DATA_out = IO_DATA_in;

  // Other names for the same wires on the sheet: DATA_in[3:0] = IO_DATA_in

  // Notes on the sheet:
  //   _
  //   _
  //   _
  //   _
  //   _
  //   _
  //   VARIABLES
  //   _
  //   _
  //   _
  //   _
  //   _
  //   |
  //   |
  //   |
  //   |
  //   |
  //   |
  //   _
  //   _
  //   _
  //   _
  //   _
  //   _
  //   _
  //   _
  //   _
  //   _
  //   _
  //   _
  //   _
  //   _
  //   _
  //   _
  //   _
  //   _
  //   _
  //   _
  //   _
  //   _
  //   IN-OUT
  //   _
  //   _
  //   _
  //   _
  //   _
  //   _
  //   _
  //   _
  //   _
  //   _
  //   _
  //   _
  //   _
  //   _
  //   _
  //   _
  //   _
  //   _
  //   _
  //   _
  //   _
  //   _
  //   _
  //   _
  //   _
  //   _
  //   _
  //   _
  //   PARSING
  //   |
  //   |
  //   |
  //   |
  //   |
  //   |
  //   |
  //   |
  //   |
  //   |
  //   |
  //   |
  //   |
  //   |
  //   |
  //   |
  //   _
  //   _
  //   _
  //   _
  //   _
  //   _
  //   _
  //   _
  //   _
  //   _
  //   _
  //   _
  //   _
  //   _
  //   _
  //   _
  //   _
  //   _
  //   _
  //   _
  //   _
  //   _
  //   _
  //   _
  //   _
  //   _
  //   _
  //   _
  //   _
  //   _
  //   _
  //   _
  //   _
  //   _
  //   _
  //   _
  //   _
  //   _
  //   _
  //   _
  //   _
  //   _
  //   _
  //   _
  //   _
  //   _
  //   _
  //   _
  //   _
  //   _
  //   _
  //   _
  //   _
  //   _
  //   _
  //   _
  //   _
  //   _
  //   _
  //   _
  //   _
  //   _
  //   _
  //   _
  //   _
  //   _
  //   _
  //   _
  //   _
  //   _
  //   _
  //   _
  //   _
  //   _
  //   _
  //   _
  //   _
  //   _
  //   _
  //   _
  //   _
  //   _
  //   _
  //   _
  //   _
  //   _
  //   _
  //   _
  //   _
  //   _
  //   _
  //   _
  //   _
  //   _
  //   _
  //   _
  //   _
  //   _
  //   _
  //   _
  //   |
  //   |
  //   |
  //   |
  //   |
  //   |
  //   _
  //   _
  //   _
  //   _
  //   _
  //   _
  //   _
  //   _
  //   _
  //   _
  //   _
  //   _
  //   _
  //   _
  //   _
  //   _
  //   _
  //   _
  //   _
  //   _
  //   _
  //   _
  //   _
  //   _
  //   |
  //   |
  //   |
  //   |
  //   |
  //   |
  //   |
  //   |
  //   |
  //   |
  //   |
  //   |
  //   |
  //   |
  //   |
  //   |
  //   _
  //   _
  //   _
  //   _
  //   _
  //   _
  //   _
  //   _
  //   _
  //   _
  //   _
  //   MEMORY
  //   _
  //   _
  //   _
  //   _
  //   _
  //   _
  //   _
  //   _
  //   _
  //   _
  //   _
  //   _
  //   _
  //   _
  //   _
  //   _
  //   _
  //   _
  //   _
  //   _
  //   _
  //   _
  //   _
  //   _
  //   _
  //   _
  //   _
  //   _
  //   _
  //   _
  //   _
  //   _
  //   _
  //   _
  //   _
  //   _
  //   _
  //   _
  //   _
  //   _
  //   _
  //   _
  //   _
  //   _
  //   _
  //   _
  //   _
  //   _
  //   _
  //   _
  //   _
  //   _
  //   _
  //   |
  //   _
  //   _
  //   |
  //   |
  //   |
  //   |
  //   |
  //   |
  //   |
  //   _
  //   _
  //   |
  //   |
  //   |
  //   |
  //   |
  //   |
  //   |
  //   |
  //   _
  //   _
  //   _
  //   _
  //   _
  //   _
  //   _
  //   _
  //   _
  //   _
  //   _
  //   OUTPUT PARSER
  //   _
  //   _
  //   _
  //   _
  //   _
  //   _
  //   OUTPUT OF CELL D4
  //   _
  //   _
  //   _
  //   _
  //   _
  //   _
  //   _
  //   _
  //   _
  //   _
  //   _
  //   _
  //   _
  //   _
  //   OUTPUT OF CELL D1
  //   _
  //   _
  //   _
  //   _
  //   _
  //   _
  //   _
  //   _
  //   _
  //   _
  //   _
  //   _
  //   _
  //   _
  //   _
  //   _
  //   _
  //   _
  //   _
  //   _
  //   _
  //   _
  //   _
  //   _
  //   _
  //   _
  //   _
  //   _
  //   _
  //   _
  //   _
  //   _
  //   _
  //   _
  //   _
  //   _
  //   _
  //   _
  //   _
  //   _
  //   _
  //   _
  //   _
  //   _
  //   _
  //   _
  //   _
  //   _
  //   _
  //   _
  //   _
  //   _
  //   _
  //   _
  //   _
  //   _
  //   _
  //   _
  //   _
  //   _
  //   _
  //   _
  //   _
  //   _
  //   _
  //   _
  //   _
  //   _
  //   _
  //   _
  //   _
  //   _
  //   _
  //   _
  //   _
  //   _
  //   _
  //   _
  //   _
  //   _
  //   _
  //   _
  //   _
  //   _
  //   _
  //   _
  //   _
  //   _
  //   _
  //   _
  //   _
  //   _
  //   _
  //   _
  //   _
  //   _
  //   _
  //   _
  //   _
  //   _
  //   _
  //   _
  //   _
  //   _
  //   _
  //   _
  //   _
  //   |
  //   _
  //   _
  //   _
  //   _
  //   _
  //   _
  //   |
  //   |
  //   |
  //   |
  //   |
  //   |
  //   |
  //   |
  //   |
  //   |
  //   |
  //   |
  //   _
  //   _
  //   _
  //   _
  //   _
  //   _
  //   _
  //   |
  //   _
  //   _
  //   _
  //   _
  //   _
  //   _
  //   |
  //   |
  //   |
  //   |
  //   |
  //   |
  //   |
  //   |
  //   |
  //   |
  //   |
  //   |
  //   |
  //   _
  //   _
  //   _
  //   _
  //   _
  //   _
  //   _
  //   _
  //   _
  //   OUTPUT OF CELL D3
  //   _
  //   _
  //   _
  //   _
  //   _
  //   _
  //   _
  //   _
  //   _
  //   _
  //   _
  //   _
  //   _
  //   _
  //   _
  //   OUTPUT OF CELL D0
  //   _
  //   _
  //   _
  //   _
  //   _
  //   _
  //   _
  //   _
  //   _
  //   _
  //   _
  //   _
  //   _
  //   _
  //   _
  //   _
  //   _
  //   _
  //   _
  //   _
  //   _
  //   _
  //   _
  //   _
  //   _
  //   _
  //   _
  //   _
  //   _
  //   _
  //   _
  //   _
  //   _
  //   _
  //   _
  //   _
  //   _
  //   _
  //   _
  //   _
  //   _
  //   _
  //   _
  //   _
  //   _
  //   _
  //   _
  //   _
  //   _
  //   _
  //   _
  //   _
  //   _
  //   _
  //   _
  //   _
  //   _
  //   _
  //   _
  //   _
  //   _
  //   _
  //   _
  //   _
  //   _
  //   _
  //   _
  //   _
  //   _
  //   _
  //   _
  //   _
  //   _
  //   _
  //   _
  //   _
  //   _
  //   _
  //   _
  //   _
  //   _
  //   _
  //   |
  //   _
  //   _
  //   _
  //   _
  //   _
  //   |
  //   |
  //   |
  //   |
  //   |
  //   |
  //   |
  //   |
  //   |
  //   |
  //   |
  //   |
  //   _
  //   _
  //   _
  //   _
  //   _
  //   _
  //   _
  //   _
  //   |
  //   |
  //   |
  //   |
  //   |
  //   |
  //   |
  //   |
  //   |
  //   |
  //   |
  //   |
  //   |
  //   |
  //   _
  //   _
  //   _
  //   _
  //   _
  //   _
  //   _
  //   _
  //   _
  //   _
  //   OUTPUT OF CELL D2
  //   _
  //   _
  //   _
  //   _
  //   _
  //   _
  //   _
  //   _
  //   _
  //   _
  //   _
  //   _
  //   _
  //   _
  //   _
  //   _
  //   _
  //   _
  //   _
  //   _
  //   _
  //   _
  //   _
  //   _
  //   _
  //   _
  //   _
  //   _
  //   _
  //   _
  //   _
  //   _
  //   _
  //   _
  //   _
  //   _
  //   _
  //   _
  //   _
  //   _
  //   _
  //   _
  //   _
  //   _
  //   _
  //   _
  //   _
  //   _
  //   _
  //   _
  //   _
  //   _
  //   _
  //   _
  //   _
  //   _
  //   _
  //   _
  //   _
  //   _
  //   _
  //   _
  //   _
  //   _
  //   _
  //   _
  //   _
  //   _
  //   _
  //   _
  //   _
  //   _
  //   _
  //   _
  //   _
  //   _
  //   _
  //   _
  //   _
  //   _
  //   _
  //   _
  //   _
  //   _
  //   _
  //   _
  //   _
  //   _
  //   |
  //   |
  //   |
  //   |
  //   |
  //   |
  //   |
  //   |
  //   _
  //   |
  //   |
  //   |
  //   |
  //   |
  //   |
  //   |
  //   |
  //   _
  //   _
  //   _
  //   _
  //   _
  //   _
  //   _
  //   _
  //   _
  //   _
  //   _
  //   OUTPUT MEMORY
  //   _
  //   _
  //   _
  //   _
  //   _
  //   _
  //   _
  //   _
  //   _
  //   _
  //   _
  //   _
  //   _
  //   _
  //   _
  //   _
  //   _
  //   _
  //   _
  //   _
  //   _
  //   _
  //   _
  //   _
  //   _
  //   _
  //   _
  //   _
  //   _
  //   _
  //   _
  //   _
  //   _
  //   _
  //   _
  //   _
  //   _
  //   _
  //   _
  //   _
  //   _
  //   _
  //   _
  //   _
  //   _
  //   _
  //   _
  //   _
  //   _
  //   _
  //   _
  //   _
  //   _
  //   _
  //   _
  //   _
  //   _
  //   _
  //   _
  //   _
  //   _
  //   _
  //   _
  //   _
  //   _
  //   _
  //   _
  //   _
  //   _
  //   _
  //   _
  //   _
  //   _
  //   _
  //   _
  //   _
  //   _
  //   _
  //   _
  //   _
  //   |
  //   |
  //   |
  //   |
  //   |
  //   |
  //   |
  //   |
  //   |
  //   |
  //   |
  //   |
  //   |
  //   |
  //   |
  //   |
endmodule

module D_trigger (
  input  SET,
  input  D,
  input  C,
  input  RESET,
  output Q,
  output NOT_Q
);

  wire nand_1_out, nand_2_out, not_1_out, not_2_out, not_3_out;

  not not_1 (not_1_out, SET);
  not not_2 (not_2_out, D);
  not not_3 (not_3_out, RESET);
  nand nand_1 (nand_1_out, D, C, not_3_out);
  nand nand_2 (nand_2_out, not_1_out, not_2_out, C);
  nand nand_3 (Q, not_1_out, nand_1_out, NOT_Q);
  nand nand_4 (NOT_Q, Q, nand_2_out, not_3_out);
endmodule

module dynamic_D_trigger (
  input  SET,
  input  D,
  input  C,
  input  RESET,
  output Q,
  output NOT_Q
);

  wire D_trigger_1_q, not_1_out;

  D_trigger D_trigger_1 (.SET(SET), .D(D), .C(C), .RESET(RESET), .Q(D_trigger_1_q));  // open: NOT_Q
  not not_1 (not_1_out, C);
  D_trigger D_trigger_2 (.SET(SET), .D(D_trigger_1_q), .C(not_1_out), .RESET(RESET), .Q(Q), .NOT_Q(NOT_Q));
endmodule

module inverse_dynamic_D_trigger (
  input  SET,
  input  D,
  input  C,
  input  RESET,
  output Q,
  output NOT_Q
);

  wire D_trigger_1_q, not_1_out;

  not not_1 (not_1_out, C);
  D_trigger D_trigger_1 (.SET(SET), .D(D), .C(not_1_out), .RESET(RESET), .Q(D_trigger_1_q));  // open: NOT_Q
  D_trigger D_trigger_2 (.SET(SET), .D(D_trigger_1_q), .C(C), .RESET(RESET), .Q(Q), .NOT_Q(NOT_Q));
endmodule

module T_trigger (
  input  SET,
  input  T,
  input  RESET,
  output Q,
  output NOT_Q
);

  dynamic_D_trigger dynamic_D_trigger_1 (.SET(SET), .D(NOT_Q), .C(T), .RESET(RESET), .Q(Q), .NOT_Q(NOT_Q));
endmodule

module D_register_4 (
  input  SET,
  input  D3,
  input  D2,
  input  D1,
  input  D0,
  input  C,
  input  RESET,
  output out_8,
  output out_9,
  output out_10,
  output out_11
);

  D_trigger d_trigger_1 (.SET(SET), .D(D3), .C(C), .RESET(RESET), .Q(out_8));  // open: NOT_Q
  D_trigger d_trigger_2 (.SET(SET), .D(D2), .C(C), .RESET(RESET), .Q(out_9));  // open: NOT_Q
  D_trigger d_trigger_3 (.SET(SET), .D(D1), .C(C), .RESET(RESET), .Q(out_10));  // open: NOT_Q
  D_trigger d_trigger_4 (.SET(SET), .D(D0), .C(C), .RESET(RESET), .Q(out_11));  // open: NOT_Q
endmodule

module dynamic_D_register_4 (
  input  SET,
  input  D3,
  input  D2,
  input  D1,
  input  D0,
  input  C,
  input  RESET,
  output Q3,
  output Q2,
  output Q1,
  output Q0
);

  inverse_dynamic_D_trigger inverse_dynamic_d_trigger_1 (
    .SET(SET), .D(D3), .C(C), .RESET(RESET), .Q(Q3));  // open: NOT_Q
  inverse_dynamic_D_trigger inverse_dynamic_d_trigger_2 (
    .SET(SET), .D(D2), .C(C), .RESET(RESET), .Q(Q2));  // open: NOT_Q
  inverse_dynamic_D_trigger inverse_dynamic_d_trigger_3 (
    .SET(SET), .D(D1), .C(C), .RESET(RESET), .Q(Q1));  // open: NOT_Q
  inverse_dynamic_D_trigger inverse_dynamic_d_trigger_4 (
    .SET(SET), .D(D0), .C(C), .RESET(RESET), .Q(Q0));  // open: NOT_Q
endmodule

module decoder_2 (
  input  A,
  output Z1,
  output Z0
);

  not not_1 (Z0, A);

  assign Z1 = A;
endmodule

module decoder_4 (
  input  S1,
  input  S0,
  output Z3,
  output Z2,
  output Z1,
  output Z0
);

  wire decoder_2_1_z0, decoder_2_1_z1, decoder_2_2_z0, decoder_2_2_z1;

  decoder_2 decoder_2_1 (.A(S1), .Z1(decoder_2_1_z1), .Z0(decoder_2_1_z0));
  decoder_2 decoder_2_2 (.A(S0), .Z1(decoder_2_2_z1), .Z0(decoder_2_2_z0));
  and and_1 (Z3, decoder_2_1_z1, decoder_2_2_z1);
  and and_2 (Z2, decoder_2_1_z1, decoder_2_2_z0);
  and and_3 (Z1, decoder_2_1_z0, decoder_2_2_z1);
  and and_4 (Z0, decoder_2_1_z0, decoder_2_2_z0);
endmodule

module decoder_8 (
  input  S2,
  input  S1,
  input  S0,
  output Z7,
  output Z6,
  output Z5,
  output Z4,
  output Z3,
  output Z2,
  output Z1,
  output Z0
);

  wire decoder_2_1_z0, decoder_2_1_z1, decoder_4_1_z0, decoder_4_1_z1, decoder_4_1_z2, decoder_4_1_z3,
       decoder_4_2_z0, decoder_4_2_z1, decoder_4_2_z2, decoder_4_2_z3;

  decoder_2 decoder_2_1 (.A(S2), .Z1(decoder_2_1_z1), .Z0(decoder_2_1_z0));
  decoder_4 decoder_4_1 (
    .S1(S1), .S0(S0), .Z3(decoder_4_1_z3), .Z2(decoder_4_1_z2), .Z1(decoder_4_1_z1), .Z0(decoder_4_1_z0));
  decoder_4 decoder_4_2 (
    .S1(S1), .S0(S0), .Z3(decoder_4_2_z3), .Z2(decoder_4_2_z2), .Z1(decoder_4_2_z1), .Z0(decoder_4_2_z0));
  and and_1 (Z7, decoder_2_1_z1, decoder_4_1_z3);
  and and_2 (Z6, decoder_2_1_z1, decoder_4_1_z2);
  and and_3 (Z5, decoder_2_1_z1, decoder_4_1_z1);
  and and_4 (Z4, decoder_2_1_z1, decoder_4_1_z0);
  and and_5 (Z3, decoder_2_1_z0, decoder_4_2_z3);
  and and_6 (Z2, decoder_2_1_z0, decoder_4_2_z2);
  and and_7 (Z1, decoder_2_1_z0, decoder_4_2_z1);
  and and_8 (Z0, decoder_2_1_z0, decoder_4_2_z0);
endmodule

module counter_mod5 (
  input  C,
  input  dec_inc,
  input  RESET,
  output Q2,
  output Q1,
  output Q0
);

  wire and_1_out, and_2_out, and_3_out, and_4_out, and_5_out, and_6_out, and_7_out, decoder_2_1_z0,
       decoder_2_1_z1, or_1_out, or_2_out, or_3_out, or_4_out, or_5_out, T_trigger_1_not_q, T_trigger_2_not_q;

  decoder_2 decoder_2_1 (.A(dec_inc), .Z1(decoder_2_1_z1), .Z0(decoder_2_1_z0));
  or or_1 (or_1_out, and_1_out, and_2_out, RESET);
  or or_2 (or_2_out, RESET, and_2_out);
  or or_3 (or_3_out, and_2_out, RESET);
  T_trigger T_trigger_1 (.SET(and_2_out), .T(C), .RESET(or_1_out), .Q(Q0), .NOT_Q(T_trigger_1_not_q));
  T_trigger T_trigger_2 (.T(or_4_out), .RESET(or_2_out), .Q(Q1), .NOT_Q(T_trigger_2_not_q));  // open: SET
  T_trigger T_trigger_3 (.SET(or_3_out), .T(and_7_out), .RESET(and_1_out), .Q(Q2));  // open: NOT_Q
  and and_1 (and_1_out, decoder_2_1_z1, Q0, T_trigger_2_not_q, Q2);
  and and_2 (and_2_out, decoder_2_1_z0, Q0, Q1, Q2);
  and and_3 (and_3_out, decoder_2_1_z1, C, Q0);
  and and_4 (and_4_out, T_trigger_1_not_q, C, decoder_2_1_z0);
  and and_5 (and_5_out, decoder_2_1_z1, Q1);
  and and_6 (and_6_out, T_trigger_2_not_q, decoder_2_1_z0);
  or or_4 (or_4_out, and_3_out, and_4_out);
  or or_5 (or_5_out, and_5_out, and_6_out);
  and and_7 (and_7_out, C, or_4_out, or_5_out);
endmodule
